# Fritzing sketch Egg Scrambling Fritzing Diagram with Mega (saved by Fritzing 0.9.3b)
breadboards: 1

parts:
  AMG8833_IR_Camera = Adafruit AMG8833 8x8 GRID EYE
  INA169_Current_Sensor = Adafruit INA169 Analog DC Current Sensor Breakout [part_number="Adafruit #1164"]
  L298N_Motor_Driver = H-Bridge with L298N
  RS-775_Blending_DC_Motor = DC Motor
  HC-SR04_Proximity_Sensor = hc-sr04
  Piezobuzzer = Piezo Speaker
  16x2_LCD_Display = LCD-16X2 [package=lcd-16x2_noholes]
  Safety_Switch = Header 2 [package=r_sw_th]
  12V_Power_Source = Power plug
  C1 = Ceramic Capacitor [capacitance="100 nF" package="0603 [SMD, multilayer]"]
  uxcell_Stirring_DC_Motor = DC Motor
  Part1 = Arduino Mega 2560 (Rev3)
  LCD_Potentiometer = Rotary Potentiometer (Small) [maximum_resistance=100kΩ package=THT]
  Blend_Button = Pushbutton [package="[THT]"]
  Stir_Button = Pushbutton [package="[THT]"]
  R1 = Resistor [tolerance=±5% resistance=220 package="2010 [SMD]"]
  R2 = Resistor [tolerance=±5% resistance=220 package="2010 [SMD]"]

nets:
  3.3V: AMG8833_IR_Camera.3.3V, Part1.3V3
  GND: AMG8833_IR_Camera.GND, INA169_Current_Sensor.GND, L298N_Motor_Driver.GND, L298N_Motor_Driver.IN4, HC-SR04_Proximity_Sensor.GND, Piezobuzzer.pin1, 12V_Power_Source.GND, Part1.GND, LCD_Potentiometer.leg2, R1.Pin_1, R2.Pin_1
  N1: AMG8833_IR_Camera.SDA, Part1.D20/SDA
  N2: AMG8833_IR_Camera.SCL, Part1.D21/SCL
  VCC: INA169_Current_Sensor.VCC, L298N_Motor_Driver.5V, L298N_Motor_Driver.IN3, HC-SR04_Proximity_Sensor.VCC, Part1.5V, LCD_Potentiometer.leg1, Blend_Button.Pin_3, Blend_Button.Pin_4, Stir_Button.Pin_3, Stir_Button.Pin_4
  N3: INA169_Current_Sensor.VIN-, C1.0, uxcell_Stirring_DC_Motor.pin_2
  N4: INA169_Current_Sensor.VIN+, L298N_Motor_Driver.M1-02
  N5: INA169_Current_Sensor.OUT, Part1.A0
  N6: L298N_Motor_Driver.12V, Safety_Switch.1
  N7: L298N_Motor_Driver.ENA, Part1.D4_PWM
  N8: L298N_Motor_Driver.IN1, Part1.D24
  N9: L298N_Motor_Driver.IN2, Part1.D26
  N10: L298N_Motor_Driver.ENB, Part1.D5_PWM
  N11: L298N_Motor_Driver.M1-01, C1.1, uxcell_Stirring_DC_Motor.pin_1
  N12: L298N_Motor_Driver.M2-01, RS-775_Blending_DC_Motor.pin_2
  N13: L298N_Motor_Driver.M2-02, RS-775_Blending_DC_Motor.pin_1
  N14: HC-SR04_Proximity_Sensor.Trig, Part1.D23
  N15: HC-SR04_Proximity_Sensor.Echo, Part1.D29
  N16: Piezobuzzer.pin2, Part1.D2_PWM
  N17: 16x2_LCD_Display.RS, Part1.D25
  N18: 16x2_LCD_Display.E, Part1.D6_PWM
  N19: 16x2_LCD_Display.DB4, Part1.D8_PWM
  N20: 16x2_LCD_Display.DB5, Part1.D27
  N21: 16x2_LCD_Display.DB6, Part1.D3_PWM
  N22: 16x2_LCD_Display.DB7, 16x2_LCD_Display.A, LCD_Potentiometer.wiper
  N23: Safety_Switch.2, 12V_Power_Source.VCC
  N24: Part1.D31, Blend_Button.Pin_1, Blend_Button.Pin_2, R2.Pin_0
  N25: Part1.D35, Stir_Button.Pin_1, Stir_Button.Pin_2, R1.Pin_0

custom parts:
  Adafruit INA169 Analog DC Current Sensor Breakout: This breakout board will solve all your current-monitoring problems. Instead of struggling with a multimeter, you can just use the handy INA169 chip on this breakout to both measure both the DC current draw and have a handy analog output that is with respect to ground. The analog output makes this an ideal breakout for feedback-loop control. Most current-measuring devices such as our current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
  H-Bridge with L298N: h-bridge
