# Fritzing sketch Egg Scrambling Fritzing Diagram (saved by Fritzing 0.9.3b)
breadboards: 1

parts:
  AMG8833_IR_Camera = Adafruit AMG8833 8x8 GRID EYE
  INA169_Current_Sensor = Adafruit INA169 Analog DC Current Sensor Breakout [part_number="Adafruit #1164"]
  L298N_Motor_Driver = H-Bridge with L298N
  RS-775_Blending_DC_Motor = DC Motor
  HC-SR04_Proximity_Sensor = hc-sr04
  Piezobuzzer = Piezo Speaker
  16x2_LCD_Display = LCD-16X2 [package=lcd-16x2_noholes]
  Arduino = Arduino Uno (Rev3)
  Power_Switch = Header 2 [package=r_sw_th]
  12V_Power_Source = Power plug
  C1 = Ceramic Capacitor [capacitance="100 nF" package="0603 [SMD, multilayer]"]
  uxcell_Stirring_DC_Motor = DC Motor

nets:
  3.3V: AMG8833_IR_Camera.3.3V, Arduino.3V3
  GND: AMG8833_IR_Camera.GND, INA169_Current_Sensor.GND, L298N_Motor_Driver.GND, L298N_Motor_Driver.IN4, HC-SR04_Proximity_Sensor.GND, Piezobuzzer.pin1, Arduino.GND, 12V_Power_Source.GND
  N1: AMG8833_IR_Camera.SDA, Arduino.A4/SDA
  N2: AMG8833_IR_Camera.SCL, Arduino.A5/SCL
  VCC: INA169_Current_Sensor.VCC, L298N_Motor_Driver.5V, L298N_Motor_Driver.IN3, HC-SR04_Proximity_Sensor.VCC, Arduino.5V
  N3: INA169_Current_Sensor.VIN-, C1.0, uxcell_Stirring_DC_Motor.pin_2
  N4: INA169_Current_Sensor.VIN+, L298N_Motor_Driver.M1-02
  N5: INA169_Current_Sensor.OUT, Arduino.A0
  N6: L298N_Motor_Driver.12V, Power_Switch.1
  N7: L298N_Motor_Driver.ENA, Arduino.D9_PWM
  N8: L298N_Motor_Driver.IN1, Arduino.D8
  N9: L298N_Motor_Driver.IN2, Arduino.D13/SCK
  N10: L298N_Motor_Driver.ENB, Arduino.D10_PWM/SS
  N11: L298N_Motor_Driver.M1-01, C1.1, uxcell_Stirring_DC_Motor.pin_1
  N12: L298N_Motor_Driver.M2-01, RS-775_Blending_DC_Motor.pin_2
  N13: L298N_Motor_Driver.M2-02, RS-775_Blending_DC_Motor.pin_1
  N14: HC-SR04_Proximity_Sensor.Trig, HC-SR04_Proximity_Sensor.Echo, Arduino.D7
  N15: Piezobuzzer.pin2, Arduino.D6_PWM
  N16: 16x2_LCD_Display.RS, Arduino.D12/MISO
  N17: 16x2_LCD_Display.E, Arduino.D11_PWM/MOSI
  N18: 16x2_LCD_Display.DB4, Arduino.D5_PWM
  N19: 16x2_LCD_Display.DB5, Arduino.D4
  N20: 16x2_LCD_Display.DB6, Arduino.D3_PWM
  N21: 16x2_LCD_Display.DB7, 16x2_LCD_Display.A, Arduino.D2
  N22: Power_Switch.2, 12V_Power_Source.VCC

custom parts:
  Adafruit INA169 Analog DC Current Sensor Breakout: This breakout board will solve all your current-monitoring problems. Instead of struggling with a multimeter, you can just use the handy INA169 chip on this breakout to both measure both the DC current draw and have a handy analog output that is with respect to ground. The analog output makes this an ideal breakout for feedback-loop control. Most current-measuring devices such as our current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
  H-Bridge with L298N: h-bridge
